# Fritzing sketch Bike_Telemetry (saved by Fritzing 0.9.3b)
perfboards: 1

parts:
  MH-ET_LIVE_ESP32_DEVKIT1 = MH-ET LIVE ESP32 DEVKIT 38 pins
  TRM1 = Terminal 2pin
  TRM2 = Terminal 2pin
  R1 = Resistor [tolerance=±5% resistance=220 package="0805 [SMD]"]
  R2 = Resistor [tolerance=±5% resistance=220 package="0402 [SMD]"]
  M1 = LJ18A3-H-ZBX [package=THT]
  U1 = LM2596 step down module
  VCC1 = Battery block 9V
  o1 = Module display OLED I2C 128x64 SSD1306 [package=THT]

nets:
  3V3: MH-ET_LIVE_ESP32_DEVKIT1.3V3, o1.VCC
  N1: MH-ET_LIVE_ESP32_DEVKIT1.GND#58, U1.IN-, U1.OUT-, VCC1.-
  N2: MH-ET_LIVE_ESP32_DEVKIT1.5V, TRM2.pin_1, M1.SIG_(BLK), U1.OUT+
  N3: MH-ET_LIVE_ESP32_DEVKIT1.GND#64, TRM1.pin_2, R1.Pin_1, M1.VO_(BLU), o1.GND
  N4: MH-ET_LIVE_ESP32_DEVKIT1.IO22, o1.SCL
  N5: MH-ET_LIVE_ESP32_DEVKIT1.IO21, o1.SDA
  N6: TRM2.pin_2, R2.Pin_0, M1.VI_(BRN)
  N7: U1.IN+, VCC1.+

custom parts:
  MH-ET LIVE ESP32 DEVKIT 38 pins: http://mh.nodebb.com/topic/2/mh-et-live-esp32-devkit
  Terminal 2pin: 2-pin Terminal Block
  LJ18A3-H-ZBX: LJ18A3-H-ZBX Proximity Sensor module.
  LM2596 step down module: LM2596 DC-DC step down power supply module 3 A.
  Module display OLED I2C 128x64 SSD1306: Ecran OLED I2C SSD163 de 128x64 avec connexion I2C
