# Fritzing sketch Diagrama_Competicao (saved by Fritzing 0.9.3b)
breadboards: 4

parts:
  Mod2 = gy-906
  M1 = LJ18A3-H-ZBX [package=THT]
  Mod3 = ossoyoo-lora-module
  M2 = LJ18A3-H-ZBX [package=THT]
  M3 = LJ18A3-H-ZBX [package=THT]
  MH-ET_LIVE_ESP32_DEVKIT1 = MH-ET LIVE ESP32 DEVKIT 38 pins
  Componente1 = LCD1602-I2C
  U1 = LM2596 step down module
  BATT1 = LiPoly Battery (1300mAh)
  R2 = Temperature Sensor (Thermistor) [thermistor_type=NTC package=THT]
  R3 = Temperature Sensor (Thermistor) [thermistor_type=NTC package=THT]
  R4 = Temperature Sensor (Thermistor) [thermistor_type=NTC package=THT]
  R5 = Resistor [tolerance=±5% resistance=220 package="2512 [SMD]"]
  R6 = Resistor [tolerance=±5% resistance=220 package="2512 [SMD]"]
  R7 = Resistor [tolerance=±5% resistance=220 package="2512 [SMD]"]
  R8 = Resistor [tolerance=±5% resistance=220 package="2512 [SMD]"]
  R9 = Temperature Sensor (Thermistor) [thermistor_type=NTC package=THT]
  U2 = Optocoupler [package=THT]
  U3 = Optocoupler [package=THT]
  U4 = Optocoupler [package=THT]
  R10 = Resistor [tolerance=±5% resistance=220 package="0805 [SMD]"]
  R11 = Resistor [tolerance=±5% resistance=220 package="0805 [SMD]"]
  R12 = Resistor [tolerance=±5% resistance=220 package="0805 [SMD]"]
  R13 = Resistor [tolerance=±5% resistance=220 package="0805 [SMD]"]
  R14 = Resistor [tolerance=±5% resistance=220 package="0805 [SMD]"]
  R15 = Resistor [tolerance=±5% resistance=220 package="0805 [SMD]"]

nets:
  VCC: Mod2.VIN, Mod3.VCC, MH-ET_LIVE_ESP32_DEVKIT1.3V3, Componente1.VCC, U2.Pin_5, U3.Pin_5, U4.Pin_5
  GND: Mod2.GND, M1.VO_(BLU), Mod3.M0, Mod3.M1, Mod3.GND, M2.VO_(BLU), M3.VO_(BLU), MH-ET_LIVE_ESP32_DEVKIT1.GND#64, Componente1.GND, U1.IN-, U1.OUT-, BATT1.negative, U2.Pin_2, U3.Pin_2, U4.Pin_2, R15.Pin_0
  N1: Mod2.SCL, MH-ET_LIVE_ESP32_DEVKIT1.IO22, Componente1.SCL
  N2: Mod2.SDA, MH-ET_LIVE_ESP32_DEVKIT1.IO21, Componente1.SDA
  N3: M1.VI_(BRN), R13.Pin_0
  N4: M1.SIG_(BLK), M2.SIG_(BLK), M3.SIG_(BLK), U1.IN+, BATT1.positive
  N5: Mod3.RXD, MH-ET_LIVE_ESP32_DEVKIT1.IO16
  N6: Mod3.TXD, MH-ET_LIVE_ESP32_DEVKIT1.IO17
  N7: M2.VI_(BRN), R14.Pin_0
  N8: M3.VI_(BRN), R15.Pin_1
  N9: MH-ET_LIVE_ESP32_DEVKIT1.IO32, U2.Pin_4, R10.Pin_0
  N10: MH-ET_LIVE_ESP32_DEVKIT1.IO33, U3.Pin_4, R11.Pin_0
  N11: MH-ET_LIVE_ESP32_DEVKIT1.IO25, R8.Pin_0, R9.pin_0
  N12: MH-ET_LIVE_ESP32_DEVKIT1.IO26, R3.pin_0, R7.Pin_0
  N13: MH-ET_LIVE_ESP32_DEVKIT1.IO27, R2.pin_0, R6.Pin_0
  N14: MH-ET_LIVE_ESP32_DEVKIT1.IO14, R4.pin_0, R5.Pin_0
  N15: MH-ET_LIVE_ESP32_DEVKIT1.IO12, U4.Pin_4, R12.Pin_0
  N16: MH-ET_LIVE_ESP32_DEVKIT1.GND#58, R10.Pin_1, R11.Pin_1, R12.Pin_1
  N17: MH-ET_LIVE_ESP32_DEVKIT1.5V, U1.OUT+
  N18: R2.pin_1, R3.pin_1, R4.pin_1, R9.pin_1
  N19: R5.Pin_1, R6.Pin_1, R7.Pin_1, R8.Pin_1
  N20: U2.Pin_1, R13.Pin_1
  N21: U3.Pin_1, R14.Pin_1

custom parts:
  gy-906: gy-906 Non-contact PIR I2C interface temperature sensor breakout board.
  LJ18A3-H-ZBX: LJ18A3-H-ZBX Proximity Sensor module.
  ossoyoo-lora-module: Osoyoo Long Distance wireless transceiver Uart LoRa Module.
  MH-ET LIVE ESP32 DEVKIT 38 pins: http://mh.nodebb.com/topic/2/mh-et-live-esp32-devkit
  LCD1602-I2C: A standard character display, usually with 2x16 characters. Comes in many colors with LCM1602 IIC attached.
  LM2596 step down module: LM2596 DC-DC step down power supply module 3 A.
  LiPoly Battery (1300mAh): Lithium Ion Polymer Battery (1300mAh)
